# Fritzing sketch mobo (saved by Fritzing 0.9.3b)
breadboards: 1

parts:
  Z80 = DIP - 40 pins [chip_label=Z80 package="DIP (Dual Inline) [THT]"]
  27C64 = IC, DIP package, 28 pins [chip_label="8K ROM"]
  U4 = SN74LS32N [package="DIP14 [THT]"]
  62256_SRAM = IC, DIP package, 28 pins [chip_label="64K SRAM"]

nets:
  N1: Z80.A11, 27C64.pin23
  N2: Z80.A12, 27C64.pin2, 62256_SRAM.pin2
  N3: Z80.A13, U4.4B, 62256_SRAM.pin26
  N4: Z80.A14, U4.4A
  N5: Z80.A15, U4.1A
  N6: Z80.D4, 27C64.pin16
  N7: Z80.D3, 27C64.pin15
  N8: Z80.D5, 27C64.pin17
  N9: Z80.D6, 27C64.pin18
  N10: Z80.D2, 27C64.pin13
  N11: Z80.D7, 27C64.pin19
  N12: Z80.D0, 27C64.pin11
  N13: Z80.D1, 27C64.pin12
  N14: Z80.MREQ, U4.2B, U4.3B
  N15: Z80.RD, U4.3A
  N16: Z80.WR, U4.2A
  N17: Z80.A0, 27C64.pin10, 62256_SRAM.pin10
  N18: Z80.A1, 27C64.pin9, 62256_SRAM.pin9
  N19: Z80.A2, 27C64.pin8, 62256_SRAM.pin8
  N20: Z80.A3, 27C64.pin6, 27C64.pin7, 62256_SRAM.pin7
  N21: Z80.A4, 62256_SRAM.pin5
  N22: Z80.A5, 27C64.pin5, 62256_SRAM.pin6
  N23: Z80.A6, 27C64.pin4, 62256_SRAM.pin4
  N24: Z80.A7, 27C64.pin3, 62256_SRAM.pin3
  N25: Z80.A8, 27C64.pin25, 62256_SRAM.pin25
  N26: Z80.A9, 27C64.pin24, 62256_SRAM.pin24
  N27: Z80.A10, 27C64.pin21, 62256_SRAM.pin21
  N28: 27C64.pin20, U4.1Y
  N29: 27C64.pin22, U4.3Y, 62256_SRAM.pin22
  N30: U4.1B, U4.4Y
  N31: U4.2Y, 62256_SRAM.pin27

custom parts:
  DIP - 40 pins: The Zilog Z80 CPU.
